# Fritzing sketch Schéma cablage projet température (saved by Fritzing 0.9.3b)
circuit board: 8.46667cm x 5.64444cm
breadboards: 1

parts:
  Composant1 = Arduino Uno (Rev3)
  T1 = LM35 Temperature Sensor [package="TO92 [THT]"]
  T2 = LM35 Temperature Sensor [package="TO92 [THT]"]

nets:
  N1: Composant1.A0, T1.Vout
  N2: Composant1.A1, T2.Vout
  GND: Composant1.GND, T1.GND, T2.GND
  N3: Composant1.5V, T1.+Vs, T2.+Vs
