# Fritzing sketch schéma câblage ADXL 335 (saved by Fritzing 0.9.3b)

parts:
  carte_arduino = Arduino Uno (Rev3)
  ADXL_335 = Triple Axis Accelerometer Breakout - ADXL335

nets:
  N1: carte_arduino.A0, ADXL_335.XOUT
  3V3: carte_arduino.3V3, ADXL_335.VCC
  GND: carte_arduino.GND, ADXL_335.GND

// code stored in the sketch: CΓblage.ino

